# Fritzing sketch report_2-circuit_1 (saved by Fritzing 0.9.3b)
breadboards: 1

parts:
  R3 = Resistor [tolerance=±5% resistance=100 package=THT]
  R5 = Resistor [tolerance=±5% resistance=510 package=THT]
  R2 = Resistor [tolerance=±5% resistance=510 package=THT]
  R1 = Resistor [tolerance=±5% resistance=220 package=THT]
  R4 = Resistor [tolerance=±5% resistance=100 package=THT]

nets:
  N1: R3.Pin_0, R5.Pin_0, R1.Pin_1, R4.Pin_0
  N2: R3.Pin_1, R2.Pin_1
  N3: R5.Pin_1, R2.Pin_0, R1.Pin_0, R4.Pin_1
